// Logisim project StackPU.circ as structural Verilog: 1 circuit, main circuit main
module main (
);

  wire and_1_out, and_10_out, and_12_out, and_13_out, and_15_out, and_16_out, and_17_out, and_18_out,
       and_19_out, and_20_out, and_21_out, and_22_out, and_23_out, and_24_out, and_25_out, and_26_out,
       and_27_out, and_28_out, and_29_out, and_30_out, button_1_out, button_2_out, button_3_out, clock_1_out,
       d_ff_1_q, d_ff_1_qn, d_ff_2_q, d_ff_3_q, decoder_1_out0, decoder_1_out1, decoder_1_out2,
       decoder_1_out3, decoder_1_out4, decoder_1_out5, decoder_1_out6, decoder_1_out7, decoder_1_out9,
       decoder_1_out10, decoder_1_out11, decoder_1_out12, decoder_1_out13, decoder_1_out14, nor_1_out,
       nor_2_out, nor_4_out, nor_5_out, not_1_out, not_2_out, or_1_out, or_3_out, or_4_out, or_5_out;
  wire [2:0] adder_2_cout, multiplexer_2_out, register_3_q;
  wire [4:0] multiplexer_2_out_2, subtractor_1_out;
  wire [6:0] or_6_out;
  wire [7:0] adder_1_out, adder_2_out, and_2_out, and_3_out, and_4_out, and_5_out, and_6_out, and_7_out,
       and_8_out, and_9_out, and_11_out, and_14_out, and_31_out, and_32_out, and_33_out, and_34_out,
       and_35_out, and_36_out, and_37_out, bit_extender_1_out, bit_extender_2_out, bit_extender_3_out,
       bit_extender_4_out, bit_extender_5_out, bit_extender_6_out, bit_extender_7_out, bit_extender_8_out,
       bit_extender_9_out, bit_extender_10_out, bit_extender_11_out, bit_extender_12_out,
       bit_extender_13_out, bit_extender_14_out, bit_extender_15_out, bit_extender_16_out, multiplexer_1_out,
       multiplexer_3_out, or_2_out, or_7_out, or_8_out, or_9_out, or_10_out, or_11_out, or_12_out,
       ram_1_dout, register_1_q, register_2_q, register_4_q, register_5_q, register_6_q, register_7_q,
       register_8_q, register_9_q, register_10_q, register_11_q, rom_1_data, shifter_1_out, subtractor_2_out,
       xor_1_out;

  ROM rom_1 (.addr(register_2_q), .data(rom_1_data));
  Register register_1 (.D(rom_1_data), .en(1'b1), .clk(clock_1_out), .Q(register_1_q));  // open: clr
  Button button_1 (.out(button_1_out));
  Register register_2 (.D(multiplexer_1_out), .en(1'b1), .clk(clock_1_out), .Q(register_2_q), .clr(button_1_out));
  Multiplexer #(.enable("false"), .width(8)) multiplexer_1 (
    .in0(adder_1_out), .in1(rom_1_data), .out(multiplexer_1_out), .sel(d_ff_2_q));
  Multiplexer #(.enable("false"), .width(8)) multiplexer_2 (
    .in0(rom_1_data), .in1(register_1_q), .out({multiplexer_2_out_2, multiplexer_2_out}), .sel(d_ff_1_q));
  Adder adder_1 (.a(register_2_q), .b(8'h1), .out(adder_1_out));  // open: cin, cout
  nor nor_1 (nor_1_out, multiplexer_2_out_2[0], multiplexer_2_out_2[1], multiplexer_2_out_2[2], multiplexer_2_out_2[3], multiplexer_2_out_2[4]);
  nor nor_2 (nor_2_out, multiplexer_2_out[0], multiplexer_2_out[1], multiplexer_2_out[2]);
  D_Flip_Flop d_ff_1 (.D(and_1_out), .clk(clock_1_out), .Q(d_ff_1_q), .Qn(d_ff_1_qn));  // open: preset, reset
  not not_1 (not_1_out, d_ff_1_q);
  LED led_1 (.in(and_3_out[7]));
  LED led_2 (.in(and_3_out[6]));
  or or_1 (or_1_out, d_ff_3_q, nor_1_out);
  Subtractor #(.width(5)) subtractor_1 (
    .a(multiplexer_2_out_2), .b(5'b00001), .out(subtractor_1_out));  // open: bin, bout
  Multiplexer #(.enable("false"), .width(8)) multiplexer_3 (
    .in0(rom_1_data), .in1(and_14_out), .out(multiplexer_3_out), .sel(not_1_out));
  LED led_3 (.in(and_3_out[5]));
  LED led_4 (.in(and_3_out[4]));
  LED led_5 (.in(and_3_out[3]));
  LED led_6 (.in(and_3_out[2]));
  not not_2 (not_2_out, or_1_out);
  Decoder #(.select(4)) decoder_1 (
    .out0(decoder_1_out0), .out1(decoder_1_out1), .out2(decoder_1_out2), .out3(decoder_1_out3),
    .out4(decoder_1_out4), .out5(decoder_1_out5), .out6(decoder_1_out6), .out7(decoder_1_out7),
    .out9(decoder_1_out9), .out10(decoder_1_out10), .out11(decoder_1_out11), .out12(decoder_1_out12),
    .out13(decoder_1_out13), .out14(decoder_1_out14), .sel(subtractor_1_out[3:0]), .en(not_2_out));  // open: out8, out15
  and and_1 (and_1_out, nor_2_out, d_ff_1_qn, nor_4_out);
  Adder adder_2 (.a(and_3_out), .b(multiplexer_3_out), .out(adder_2_out), .cin(decoder_1_out5), .cout(adder_2_cout[0]));
  Subtractor subtractor_2 (
    .a(and_3_out), .b(multiplexer_3_out), .out(subtractor_2_out), .bin(decoder_1_out7));  // open: bout
  assign xor_1_out = and_3_out ^ multiplexer_3_out;  // XOR_Gate xor_1, 8 bits wide
  assign and_2_out = and_3_out & multiplexer_3_out;  // AND_Gate and_2, 8 bits wide
  assign or_2_out = and_3_out | multiplexer_3_out;  // OR_Gate or_2, 8 bits wide
  Shifter #(.shift("lr")) shifter_1 (.in(and_3_out), .\dist (3'b001), .out(shifter_1_out));
  LED led_7 (.in(and_3_out[1]));
  LED led_8 (.in(and_3_out[0]));
  nor nor_3 (adder_2_cout[2], or_6_out[0], or_6_out[1], or_6_out[2], or_6_out[3], or_6_out[4], or_6_out[5], or_6_out[6], adder_2_cout[1]);
  RAM #(.asyncread("true")) ram_1 (
    .addr(or_7_out), .we(decoder_1_out14), .clk(decoder_1_out13), .din(and_3_out), .dout(ram_1_dout));  // open: oe
  Clock clock_1 (.out(clock_1_out));
  or or_3 (or_3_out, decoder_1_out0, decoder_1_out1, decoder_1_out2, decoder_1_out3, decoder_1_out4, decoder_1_out10);
  assign bit_extender_1_out = {{7{or_4_out}}, or_4_out};  // Bit_Extender bit_extender_1
  or or_4 (or_4_out, decoder_1_out0, decoder_1_out5, decoder_1_out9, decoder_1_out10);
  assign bit_extender_2_out = {{7{or_5_out}}, or_5_out};  // Bit_Extender bit_extender_2
  or or_5 (or_5_out, decoder_1_out7, decoder_1_out1);
  assign bit_extender_3_out = {{7{decoder_1_out2}}, decoder_1_out2};  // Bit_Extender bit_extender_3
  assign bit_extender_4_out = {{7{decoder_1_out3}}, decoder_1_out3};  // Bit_Extender bit_extender_4
  assign bit_extender_5_out = {{7{decoder_1_out4}}, decoder_1_out4};  // Bit_Extender bit_extender_5
  assign bit_extender_6_out = {{7{decoder_1_out6}}, decoder_1_out6};  // Bit_Extender bit_extender_6
  assign bit_extender_7_out = {{7{decoder_1_out10}}, decoder_1_out10};  // Bit_Extender bit_extender_7
  assign and_3_out = ~bit_extender_7_out & register_4_q;  // AND_Gate and_3, 8 bits wide
  D_Flip_Flop d_ff_2 (.D(and_12_out), .clk(clock_1_out), .Q(d_ff_2_q));  // open: Qn, preset, reset
  D_Flip_Flop d_ff_3 (.D(decoder_1_out11), .clk(clock_1_out), .Q(d_ff_3_q));  // open: Qn, preset, reset
  nor nor_4 (nor_4_out, decoder_1_out14, decoder_1_out12, or_1_out, decoder_1_out11, decoder_1_out9);
  assign and_4_out = bit_extender_1_out & adder_2_out;  // AND_Gate and_4, 8 bits wide
  assign and_5_out = bit_extender_2_out & subtractor_2_out;  // AND_Gate and_5, 8 bits wide
  assign and_6_out = bit_extender_3_out & xor_1_out;  // AND_Gate and_6, 8 bits wide
  assign and_7_out = bit_extender_4_out & and_2_out;  // AND_Gate and_7, 8 bits wide
  assign and_8_out = bit_extender_5_out & or_2_out;  // AND_Gate and_8, 8 bits wide
  assign and_9_out = bit_extender_6_out & shifter_1_out;  // AND_Gate and_9, 8 bits wide
  assign bit_extender_8_out = {{7{decoder_1_out13}}, decoder_1_out13};  // Bit_Extender bit_extender_8
  and and_10 (and_10_out, nor_4_out, ~and_1_out);  // AND_Gate
  assign {adder_2_cout[1], or_6_out} = and_4_out | and_5_out | and_6_out | and_11_out | and_7_out | and_8_out | and_9_out;  // OR_Gate or_6, 8 bits wide
  assign and_11_out = bit_extender_8_out & ram_1_dout;  // AND_Gate and_11, 8 bits wide
  and and_12 (and_12_out, decoder_1_out11, nor_5_out);
  and and_13 (and_13_out, multiplexer_2_out[2], ~register_3_q[2]);  // AND_Gate
  Register #(.width(3)) register_3 (
    .D(adder_2_cout), .en(and_10_out), .clk(clock_1_out), .Q(register_3_q));  // open: clr
  assign bit_extender_9_out = {{7{or_3_out}}, or_3_out};  // Bit_Extender bit_extender_9
  assign and_14_out = bit_extender_9_out & or_7_out;  // AND_Gate and_14, 8 bits wide
  Register register_4 (
    .D({adder_2_cout[1], or_6_out}), .en(and_10_out), .clk(clock_1_out), .Q(register_4_q), .clr(button_2_out));
  Button button_2 (.out(button_2_out));
  nor nor_5 (nor_5_out, and_13_out, and_15_out, and_16_out);
  and and_15 (and_15_out, multiplexer_2_out[1], ~register_3_q[1]);  // AND_Gate
  and and_16 (and_16_out, multiplexer_2_out[0], ~register_3_q[0]);  // AND_Gate
  Register register_5 (
    .D({adder_2_cout[1], or_6_out}), .en(and_17_out), .clk(clock_1_out), .Q(register_5_q), .clr(button_3_out));
  and and_17 (and_17_out, decoder_1_out9, and_18_out);
  and and_18 (and_18_out, multiplexer_2_out[0], ~multiplexer_2_out[1], ~multiplexer_2_out[2]);  // AND_Gate
  Register register_6 (
    .D({adder_2_cout[1], or_6_out}), .en(and_19_out), .clk(clock_1_out), .Q(register_6_q), .clr(button_3_out));
  and and_19 (and_19_out, decoder_1_out9, and_20_out);
  and and_20 (and_20_out, ~multiplexer_2_out[0], multiplexer_2_out[1], ~multiplexer_2_out[2]);  // AND_Gate
  Register register_7 (
    .D({adder_2_cout[1], or_6_out}), .en(and_21_out), .clk(clock_1_out), .Q(register_7_q), .clr(button_3_out));
  and and_21 (and_21_out, decoder_1_out9, and_22_out);
  and and_22 (and_22_out, multiplexer_2_out[0], multiplexer_2_out[1], ~multiplexer_2_out[2]);  // AND_Gate
  Register register_8 (
    .D({adder_2_cout[1], or_6_out}), .en(and_23_out), .clk(clock_1_out), .Q(register_8_q), .clr(button_3_out));
  and and_23 (and_23_out, decoder_1_out9, and_24_out);
  and and_24 (and_24_out, ~multiplexer_2_out[0], ~multiplexer_2_out[1], multiplexer_2_out[2]);  // AND_Gate
  Register register_9 (
    .D({adder_2_cout[1], or_6_out}), .en(and_25_out), .clk(clock_1_out), .Q(register_9_q), .clr(button_3_out));
  and and_25 (and_25_out, decoder_1_out9, and_26_out);
  and and_26 (and_26_out, multiplexer_2_out[0], ~multiplexer_2_out[1], multiplexer_2_out[2]);  // AND_Gate
  Register register_10 (
    .D({adder_2_cout[1], or_6_out}), .en(and_27_out), .clk(clock_1_out), .Q(register_10_q), .clr(button_3_out));
  and and_27 (and_27_out, decoder_1_out9, and_28_out);
  and and_28 (and_28_out, ~multiplexer_2_out[0], multiplexer_2_out[1], multiplexer_2_out[2]);  // AND_Gate
  Register register_11 (
    .D({adder_2_cout[1], or_6_out}), .en(and_29_out), .clk(clock_1_out), .Q(register_11_q), .clr(button_3_out));
  and and_29 (and_29_out, decoder_1_out9, and_30_out);
  and and_30 (and_30_out, multiplexer_2_out[0], multiplexer_2_out[1], multiplexer_2_out[2]);
  assign and_31_out = register_5_q & bit_extender_10_out;  // AND_Gate and_31, 8 bits wide
  assign bit_extender_10_out = {{7{and_18_out}}, and_18_out};  // Bit_Extender bit_extender_10
  assign and_32_out = register_6_q & bit_extender_11_out;  // AND_Gate and_32, 8 bits wide
  assign bit_extender_11_out = {{7{and_20_out}}, and_20_out};  // Bit_Extender bit_extender_11
  assign and_33_out = register_7_q & bit_extender_12_out;  // AND_Gate and_33, 8 bits wide
  assign bit_extender_12_out = {{7{and_22_out}}, and_22_out};  // Bit_Extender bit_extender_12
  assign and_34_out = register_8_q & bit_extender_13_out;  // AND_Gate and_34, 8 bits wide
  assign bit_extender_13_out = {{7{and_24_out}}, and_24_out};  // Bit_Extender bit_extender_13
  assign and_35_out = register_9_q & bit_extender_14_out;  // AND_Gate and_35, 8 bits wide
  assign bit_extender_14_out = {{7{and_26_out}}, and_26_out};  // Bit_Extender bit_extender_14
  assign and_36_out = register_10_q & bit_extender_15_out;  // AND_Gate and_36, 8 bits wide
  assign bit_extender_15_out = {{7{and_28_out}}, and_28_out};  // Bit_Extender bit_extender_15
  assign and_37_out = register_11_q & bit_extender_16_out;  // AND_Gate and_37, 8 bits wide
  assign bit_extender_16_out = {{7{and_30_out}}, and_30_out};  // Bit_Extender bit_extender_16
  assign or_7_out = and_31_out | or_8_out;  // OR_Gate or_7, 8 bits wide
  assign or_8_out = and_32_out | or_9_out;  // OR_Gate or_8, 8 bits wide
  assign or_9_out = and_33_out | or_10_out;  // OR_Gate or_9, 8 bits wide
  assign or_10_out = and_34_out | or_11_out;  // OR_Gate or_10, 8 bits wide
  Button button_3 (.out(button_3_out));
  assign or_11_out = and_35_out | or_12_out;  // OR_Gate or_11, 8 bits wide
  assign or_12_out = and_36_out | and_37_out;  // OR_Gate or_12, 8 bits wide

  // Notes on the sheet:
  //   contents of rom_1 (hex, n*v repeats v):
  //   49 51 31 54 71 52 74 53 12 62 15 5c 51 31 54 10 8 64 1b 60 4 5b 79 5a 7c 60 b 49 51 54 60 4
  //   zero operand
  //   acc write
endmodule
